# Fritzing sketch wearableSensor (saved by Fritzing 0.9.4)

parts:
  Part2 = 16 NeoPixel Ring [part_number=1463]
  Part3 = Adafruit USB LiIon/LiPoly Charger [part_number="Adafruit #259"]  # not connected
  Part4 = Lithium Ion Polymer Battery 3.7v 500mAh [part_number=1578]  # not connected
  IC1 = SO08-EIAJ [chip_label=SO08-EIAJ package=SO]
  Part1 = Arduino Nano (Rev3.0)

nets:
  N1: Part2.IN, Part1.D5
  GND: Part2.GND, IC1.4, Part1.GND
  VDD: Part2.VDD, IC1.3, Part1.3V3
  N2: IC1.1, Part1.A0
  N3: IC1.2, Part1.D8

custom parts:
  16 NeoPixel Ring: 16 ultra bright smart LED NeoPixels are arranged in a circle with 1.75" (44.5mm) outer diameter. The rings are 'chainable' - connect the output pin of one to the input pin of another. Use only one microcontroller pin to control as many as you can chain together! Each LED is addressable as the driver chip is inside the LED. Each one has ~18mA constant current drive so the color will be very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
  Adafruit USB LiIon/LiPoly Charger: This is a Lithium Ion and Lithium Polymer battery charger based on the MCP73833. It uses a USB mini-B for connection to any computer or 'USB wall adapter'. Charging is performed in three stages: first a preconditioning charge, then a constant-current fast charge and finally a constant-voltage trickle charge to keep the battery topped-up. The fast-charge current is 500mA by default, but is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
  Lithium Ion Polymer Battery 3.7v 500mAh: Lithium ion polymer (also known as 'lipo' or 'lipoly') batteries are thin, light and powerful. The output ranges from 4.2V when completely charged to 3.7V. This battery has a capacity of 500mAh for a total of about 1.9 Wh. The batteries come pre-attached with a genuine 2-pin JST-PH connector as shown and include the necessary protection circuitry.
